// Logisim project ALU.circ as structural Verilog
module ALU (
  input  isAdd,
  input  isSub,
  input  [31:0] op1,
  input  isMul,
  input  isDiv,
  input  [31:0] op2,
  input  isMod,
  input  isimmediate,
  input  isLsl,
  input  [2:0] in_10,
  input  isLsr,
  input  [31:0] immx,
  input  [2:0] in_13,
  input  isAsr,
  input  [2:0] in_15,
  input  isAnd,
  input  isOr,
  input  isAnd_2,
  input  isMov,
  input  in_20,
  input  isCmp,
  input  in_22,
  input  isCmp_2,
  input  isUbranch,
  input  isbgt,
  input  isbeq,
  output [31:0] AluReasult,
  output isBranchTaken
);

  wire comparator_1_gt, comparator_2_eq, E, GT, multiplexer_2_out, multiplexer_3_out;
  wire [4:0] bitselector_1_out, bitselector_2_out, bitselector_3_out;
  wire [31:0] adder_1_out, and_1_out, b, divider_1_out, divider_1_rem, multiplier_1_out, negator_1_out,
       or_1_out, shifter_1_out, shifter_2_out, shifter_3_out, subtractor_1_out;

  Multiplexer #(.width(32)) multiplexer_1 (.in0(op2), .in1(immx), .out(b), .sel(isimmediate));  // open: en
  Comparator #(.width(32)) comparator_1 (.a(op1), .b(b), .gt(comparator_1_gt));  // open: eq, lt
  Comparator #(.width(32)) comparator_2 (.a(op1), .b(b), .eq(comparator_2_eq));  // open: gt, lt
  Multiplexer multiplexer_2 (.in0(GT), .in1(comparator_1_gt), .out(multiplexer_2_out), .sel(isCmp));  // open: en
  Multiplexer multiplexer_3 (.in0(E), .in1(comparator_2_eq), .out(multiplexer_3_out), .sel(isCmp_2));  // open: en
  BitSelector #(.width(32), .group(5)) bitselector_1 (.in(b), .out(bitselector_1_out), .sel(in_10));
  BitSelector #(.width(32), .group(5)) bitselector_2 (.in(b), .out(bitselector_2_out), .sel(in_13));
  BitSelector #(.width(32), .group(5)) bitselector_3 (.in(b), .out(bitselector_3_out), .sel(in_15));
  branchUnit branchunit_1 (
    .isUbranch(isUbranch), .GT(GT), .isbgt(isbgt), .E(E), .isbeq(isbeq), .isBranchTaken(isBranchTaken));
  Adder #(.width(32)) adder_1 (.a(op1), .b(b), .out(adder_1_out));  // open: cin, cout
  Subtractor #(.width(32)) subtractor_1 (.a(op1), .b(b), .out(subtractor_1_out));  // open: bin, bout
  Multiplier #(.width(32)) multiplier_1 (.a(op1), .b(b), .out(multiplier_1_out));  // open: cin, cout
  Divider #(.width(32)) divider_1 (.a(op1), .b(b), .out(divider_1_out), .rem(divider_1_rem));  // open: upper
  Shifter #(.width(32)) shifter_1 (.in(op1), .\dist (bitselector_1_out), .out(shifter_1_out));
  Shifter #(.width(32), .shift("lr")) shifter_2 (.in(op1), .\dist (bitselector_2_out), .out(shifter_2_out));
  Shifter #(.width(32), .shift("ar")) shifter_3 (.in(op1), .\dist (bitselector_3_out), .out(shifter_3_out));
  assign and_1_out = op1 & b;  // AND_Gate and_1, 32 bits wide
  assign or_1_out = op1 | b;  // OR_Gate or_1, 32 bits wide
  Negator #(.width(32)) negator_1 (.out(negator_1_out));  // open: in
  D_Flip_Flop #(.trigger("high")) d_ff_1 (.clk(in_20), .D(multiplexer_2_out), .Q(GT));  // open: Qn, preset, en, reset
  D_Flip_Flop #(.trigger("high")) d_ff_2 (.clk(in_22), .D(multiplexer_3_out), .Q(E));  // open: Qn, preset, en, reset
  assign AluReasult = isMul ? multiplier_1_out : 32'bz;  // Controlled_Buffer controlled_buffer_1
  assign AluReasult = isDiv ? divider_1_out : 32'bz;  // Controlled_Buffer controlled_buffer_2
  assign AluReasult = isMod ? divider_1_rem : 32'bz;  // Controlled_Buffer controlled_buffer_3
  assign AluReasult = isLsl ? shifter_1_out : 32'bz;  // Controlled_Buffer controlled_buffer_4
  assign AluReasult = isLsr ? shifter_2_out : 32'bz;  // Controlled_Buffer controlled_buffer_5
  assign AluReasult = isAsr ? shifter_3_out : 32'bz;  // Controlled_Buffer controlled_buffer_6
  assign AluReasult = isAnd ? and_1_out : 32'bz;  // Controlled_Buffer controlled_buffer_7
  assign AluReasult = isOr ? or_1_out : 32'bz;  // Controlled_Buffer controlled_buffer_8
  assign AluReasult = isAnd_2 ? negator_1_out : 32'bz;  // Controlled_Buffer controlled_buffer_9
  assign AluReasult = isMov ? b : 32'bz;  // Controlled_Buffer controlled_buffer_10
  assign AluReasult = isAdd ? adder_1_out : 32'bz;  // Controlled_Buffer controlled_buffer_11
  assign AluReasult = isSub ? subtractor_1_out : 32'bz;  // Controlled_Buffer controlled_buffer_12

  // Other names for the same wires on the sheet: a[31:0] = op1
endmodule

module branchUnit (
  input  isUbranch,
  input  GT,
  input  isbgt,
  input  E,
  input  isbeq,
  output isBranchTaken
);

  wire and_1_out, and_2_out;

  and and_1 (and_1_out, GT, isbgt);
  and and_2 (and_2_out, E, isbeq);
  or or_1 (isBranchTaken, isUbranch, and_1_out, and_2_out);
endmodule
