// Logisim project assn3_devansh.circ as structural Verilog: 10 circuits, main circuit main
module main (
  output [31:0] out_1,
  output [31:0] out_2,
  output [3:0] out_3,
  output [31:0] out_4,
  output [31:0] out_5,
  output [31:0] out_6,
  output [31:0] out_7,
  output [31:0] out_8,
  output [31:0] out_9,
  output [31:0] out_10
);

  wire isbeq, isbgt, isBranch, isCall, isimm, isLd, isRet, isSt, isUbranch, isWb;
  wire [3:0] rd;
  wire [12:0] ALU_Signals;
  wire [31:0] Imm_and_Branch_immx, MAStage_ldresult;

  Clock clock_1 ();  // open: out
  IFStage IFStage (.BranchTarget(out_8), .isBranchTaken(isBranch), .instruction(out_9), .pc(out_2));
  immAndBranchUnit Imm_and_Branch (
    .instruction(out_9), .pc(out_2), .value_of_ra(out_4), .isRet(isRet), .immx(Imm_and_Branch_immx),
    .BranchTarget(out_8));
  Control_Unit Control_Unit (
    .I_bit(out_9[26]), .opcode(out_9[31:27]), .isSt(isSt), .isLd(isLd), .isBeq(isbeq), .isBgt(isbgt),
    .isRet(isRet), .isImmediate(isimm), .isWb(isWb), .isUbranch(isUbranch), .isCall(isCall),
    .ALUsignals(ALU_Signals));
  Multiplexer #(.width(32), .enable("false")) multiplexer_1 (
    .in0(out_5), .in1(Imm_and_Branch_immx), .out(out_6), .sel(isimm));
  OFStage OFStage (
    .Result(out_1), .Instruction(out_9), .isWb(isWb), .rd(rd), .isRet(isRet), .isStore(isSt), .\reg (out_3),
    .op1(out_4), .op2(out_5));  // open: memoryload
  MAStage MAStage (.MDR(out_5), .isSt(isSt), .MAR(out_10), .ldResult(MAStage_ldresult));
  ALU ALU (
    .AluReasult(out_10), .isUbranch(isUbranch), .isbgt(isbgt), .isbeq(isbeq), .isBranchTaken(isBranch),
    .op1(out_4), .op2(out_6), .ALu_Signals(ALU_Signals));
  RWStage RWStage (
    .aluResult(out_10), .ldResult(MAStage_ldresult), .isLd(isLd), .pc(out_2), .isCall(isCall), .rd(rd),
    .Result(out_1), .\reg (out_3));

  assign out_7 = out_5;

  // Other names for the same wires on the sheet: A[31:0] = out_4; AluResult[31:0] = out_10; B[31:0] = out_6;
  //   BranchTarget[31:0] = out_8; Instruction[31:0] = out_9; op2[31:0] = out_5; pc[31:0] = out_2; reg[3:0] = out_3;
  //   Result[31:0] = out_1
endmodule

module ALU (
  input  [12:0] ALu_Signals,
  input  [31:0] op1,
  input  [31:0] op2,
  input  isUbranch,
  input  isbgt,
  input  isbeq,
  output [31:0] AluReasult,
  output isBranchTaken
);

  wire comparator_1_gt, comparator_2_eq, E, GT, multiplexer_1_out, multiplexer_2_out;
  wire [4:0] bitselector_1_out, bitselector_2_out, bitselector_3_out;
  wire [31:0] adder_1_out, and_1_out, divider_1_out, divider_1_rem, multiplier_1_out, negator_1_out,
       or_1_out, shifter_1_out, shifter_2_out, shifter_3_out, subtractor_1_out;

  Clock clock_1 ();  // open: out
  Comparator #(.width(32)) comparator_1 (.a(op1), .b(op2), .gt(comparator_1_gt));  // open: eq, lt
  Comparator #(.width(32)) comparator_2 (.a(op1), .b(op2), .eq(comparator_2_eq));  // open: gt, lt
  Multiplexer multiplexer_1 (
    .in0(GT), .in1(comparator_1_gt), .out(multiplexer_1_out), .sel(ALu_Signals[0]));  // open: en
  Multiplexer multiplexer_2 (
    .in0(E), .in1(comparator_2_eq), .out(multiplexer_2_out), .sel(ALu_Signals[0]));  // open: en
  BitSelector #(.width(32), .group(5)) bitselector_1 (.in(op2), .out(bitselector_1_out), .sel(3'b000));
  BitSelector #(.width(32), .group(5)) bitselector_2 (.in(op2), .out(bitselector_2_out), .sel(3'b000));
  BitSelector #(.width(32), .group(5)) bitselector_3 (.in(op2), .out(bitselector_3_out), .sel(3'b000));
  branchUnit branchunit_1 (
    .isUbranch(isUbranch), .GT(GT), .isbgt(isbgt), .E(E), .isbeq(isbeq), .isBranchTaken(isBranchTaken));
  Adder #(.width(32)) adder_1 (.a(op1), .b(op2), .out(adder_1_out));  // open: cin, cout
  Subtractor #(.width(32)) subtractor_1 (.a(op1), .b(op2), .out(subtractor_1_out));  // open: bin, bout
  Multiplier #(.width(32)) multiplier_1 (.a(op1), .b(op2), .out(multiplier_1_out));  // open: cin, cout
  Divider #(.width(32)) divider_1 (.a(op1), .b(op2), .out(divider_1_out), .rem(divider_1_rem));  // open: upper
  Shifter #(.width(32)) shifter_1 (.in(op1), .\dist (bitselector_1_out), .out(shifter_1_out));
  Shifter #(.width(32), .shift("lr")) shifter_2 (.in(op1), .\dist (bitselector_2_out), .out(shifter_2_out));
  Shifter #(.width(32), .shift("ar")) shifter_3 (.in(op1), .\dist (bitselector_3_out), .out(shifter_3_out));
  assign and_1_out = op1 & op2;  // AND_Gate and_1, 32 bits wide
  assign or_1_out = op1 | op2;  // OR_Gate or_1, 32 bits wide
  Negator #(.width(32)) negator_1 (.in(op1), .out(negator_1_out));
  D_Flip_Flop #(.trigger("low")) d_ff_1 (.clk(1'b0), .D(multiplexer_1_out), .Q(GT));  // open: Qn, preset, en, reset
  D_Flip_Flop #(.trigger("low")) d_ff_2 (.clk(1'b0), .D(multiplexer_2_out), .Q(E));  // open: Qn, preset, en, reset
  assign AluReasult = ALu_Signals[3] ? multiplier_1_out : 32'bz;  // Controlled_Buffer controlled_buffer_1
  assign AluReasult = ALu_Signals[4] ? divider_1_out : 32'bz;  // Controlled_Buffer controlled_buffer_2
  assign AluReasult = ALu_Signals[5] ? divider_1_rem : 32'bz;  // Controlled_Buffer controlled_buffer_3
  assign AluReasult = ALu_Signals[7] ? shifter_1_out : 32'bz;  // Controlled_Buffer controlled_buffer_4
  assign AluReasult = ALu_Signals[8] ? shifter_2_out : 32'bz;  // Controlled_Buffer controlled_buffer_5
  assign AluReasult = ALu_Signals[9] ? shifter_3_out : 32'bz;  // Controlled_Buffer controlled_buffer_6
  assign AluReasult = ALu_Signals[11] ? and_1_out : 32'bz;  // Controlled_Buffer controlled_buffer_7
  assign AluReasult = ALu_Signals[12] ? or_1_out : 32'bz;  // Controlled_Buffer controlled_buffer_8
  assign AluReasult = ALu_Signals[10] ? negator_1_out : 32'bz;  // Controlled_Buffer controlled_buffer_9
  assign AluReasult = ALu_Signals[6] ? op2 : 32'bz;  // Controlled_Buffer controlled_buffer_10
  assign AluReasult = ALu_Signals[1] ? adder_1_out : 32'bz;  // Controlled_Buffer controlled_buffer_11
  assign AluReasult = ALu_Signals[2] ? subtractor_1_out : 32'bz;  // Controlled_Buffer controlled_buffer_12

  // Other names for the same wires on the sheet: a[31:0] = op1; isCmp = ALu_Signals[0]; isAdd = ALu_Signals[1];
  //   isSub = ALu_Signals[2]; isMul = ALu_Signals[3]; isDiv = ALu_Signals[4]; isMod = ALu_Signals[5];
  //   isMov = ALu_Signals[6]; isLsl = ALu_Signals[7]; isLsr = ALu_Signals[8]; isAsr = ALu_Signals[9];
  //   isNot = ALu_Signals[10]; isAnd = ALu_Signals[11]; isOr = ALu_Signals[12]; b[31:0] = op2
endmodule

module branchUnit (
  input  isUbranch,
  input  GT,
  input  isbgt,
  input  E,
  input  isbeq,
  output isBranchTaken
);

  wire and_1_out, and_2_out;

  and and_1 (and_1_out, GT, isbgt);
  and and_2 (and_2_out, E, isbeq);
  or or_1 (isBranchTaken, isUbranch, and_1_out, and_2_out);
endmodule

module Control_Unit (
  input  I_bit,
  input  [4:0] opcode,
  output isSt,
  output isLd,
  output isBeq,
  output isBgt,
  output isRet,
  output isImmediate,
  output isWb,
  output isUbranch,
  output isCall,
  output [12:0] ALUsignals
);

  wire and_6_out, and_7_out, and_8_out, and_9_out, and_10_out, and_12_out, and_13_out, nand_1_out;

  nand nand_1 (nand_1_out, opcode[0], opcode[1]);
  and and_1 (isSt, opcode[0], opcode[1], opcode[2], opcode[3], ~opcode[4]);  // AND_Gate
  and and_2 (isLd, ~opcode[0], opcode[1], opcode[2], opcode[3], ~opcode[4]);  // AND_Gate
  and and_3 (isBeq, ~opcode[0], ~opcode[1], ~opcode[2], ~opcode[3], opcode[4]);  // AND_Gate
  and and_4 (isBgt, opcode[0], ~opcode[1], ~opcode[2], ~opcode[3], opcode[4]);  // AND_Gate
  and and_5 (isRet, ~opcode[0], ~opcode[1], opcode[2], ~opcode[3], opcode[4]);  // AND_Gate
  and and_6 (and_6_out, opcode[0], ~opcode[1], opcode[2], ~opcode[4]);  // AND_Gate
  and and_7 (and_7_out, opcode[0], opcode[2], opcode[3], ~opcode[4]);  // AND_Gate
  and and_8 (and_8_out, opcode[4], nand_1_out);
  and and_9 (and_9_out, opcode[1], ~opcode[2], ~opcode[3], opcode[4]);  // AND_Gate
  and and_10 (and_10_out, ~opcode[0], ~opcode[1], opcode[2], ~opcode[3], opcode[4]);  // AND_Gate
  and and_11 (isCall, opcode[0], opcode[1], ~opcode[2], ~opcode[3], opcode[4]);  // AND_Gate
  and and_12 (and_12_out, ~opcode[0], ~opcode[1], ~opcode[2], ~opcode[3], ~opcode[4]);  // AND_Gate
  and and_13 (and_13_out, opcode[1], opcode[2], opcode[3], ~opcode[4]);  // AND_Gate
  and isSub (ALUsignals[2], opcode[0], ~opcode[1], ~opcode[2], ~opcode[3], ~opcode[4]);  // AND_Gate
  and isCmp (ALUsignals[0], opcode[0], ~opcode[1], opcode[2], ~opcode[3], ~opcode[4]);  // AND_Gate
  and isMul (ALUsignals[3], ~opcode[0], opcode[1], ~opcode[2], ~opcode[3], ~opcode[4]);  // AND_Gate
  and isDiv (ALUsignals[4], opcode[0], opcode[1], ~opcode[2], ~opcode[3], ~opcode[4]);  // AND_Gate
  and isMod (ALUsignals[5], ~opcode[0], ~opcode[1], opcode[2], ~opcode[3], ~opcode[4]);  // AND_Gate
  and isLsl (ALUsignals[7], ~opcode[0], opcode[1], ~opcode[2], opcode[3], ~opcode[4]);  // AND_Gate
  and isLsr (ALUsignals[8], opcode[0], opcode[1], ~opcode[2], opcode[3], ~opcode[4]);  // AND_Gate
  and isAsr (ALUsignals[9], ~opcode[0], ~opcode[1], opcode[2], opcode[3], ~opcode[4]);  // AND_Gate
  and isOr (ALUsignals[12], opcode[0], opcode[1], opcode[2], ~opcode[3], ~opcode[4]);  // AND_Gate
  and isAnd (ALUsignals[11], ~opcode[0], opcode[1], opcode[2], ~opcode[3], ~opcode[4]);  // AND_Gate
  and isNot (ALUsignals[10], ~opcode[0], ~opcode[1], ~opcode[2], opcode[3], ~opcode[4]);  // AND_Gate
  and isMov (ALUsignals[6], opcode[0], ~opcode[1], ~opcode[2], opcode[3], ~opcode[4]);  // AND_Gate
  nor nor_1 (isWb, and_6_out, and_7_out, and_8_out);
  or or_1 (isUbranch, and_9_out, and_10_out);
  or isAdd (ALUsignals[1], and_12_out, and_13_out);

  assign isImmediate = I_bit;

  // Notes on the sheet:
  //   op1
  //   op2
  //   op3
  //   op4
  //   op5
endmodule

module immAndBranchUnit (
  input  [31:0] instruction,
  input  [31:0] pc,
  input  [31:0] value_of_ra,
  input  isRet,
  output [31:0] immx,
  output [31:0] BranchTarget
);

  wire [31:0] adder_1_out, bit_extender_2_out;

  assign immx = {{14{instruction[17]}}, instruction[17:0]};  // Bit_Extender bit_extender_1
  assign bit_extender_2_out = {{3{instruction[26]}}, {instruction[26:0], 2'b00}};  // Bit_Extender bit_extender_2
  Adder #(.width(32)) adder_1 (.a(bit_extender_2_out), .b(pc), .out(adder_1_out));  // open: cin, cout
  Multiplexer #(.width(32)) multiplexer_1 (
    .in0(adder_1_out), .in1(value_of_ra), .out(BranchTarget), .sel(isRet));  // open: en
endmodule

module IFStage (
  input  [31:0] BranchTarget,
  input  isBranchTaken,
  output [31:0] instruction,
  output [31:0] pc
);

  wire clock_1_out, nor_1_out;
  wire [1:0] mod_3_counter_q;
  wire [31:0] adder_1_out, multiplexer_1_out;

  Clock clock_1 (.out(clock_1_out));
  Counter #(.width(2), .max('h2)) mod_3_counter (
    .Q(mod_3_counter_q), .clk(clock_1_out));  // open: load, D, count, carry, clr
  Register #(.width(32)) register_1 (.D(multiplexer_1_out), .Q(pc), .clk(nor_1_out));  // open: en, clr
  nor nor_1 (nor_1_out, mod_3_counter_q[0], mod_3_counter_q[1]);
  Multiplexer #(.width(32), .enable("false")) multiplexer_1 (
    .in0(adder_1_out), .in1(BranchTarget), .out(multiplexer_1_out), .sel(isBranchTaken));
  Adder #(.width(32)) adder_1 (.a(32'h4), .b(pc), .out(adder_1_out));  // open: cin, cout
  ROM #(.addrWidth(10), .dataWidth(32)) rom_1 (.addr(pc[11:2]), .data(instruction));  // open: sel

  // Notes on the sheet:
  //   contents of rom_1 (hex, n*v repeats v):
  //   4c000004 98000002 90000000 2c000001 88000003 4c400001 a0000000 fb80008 7c380000 7ff80004 c000001
  //   9ffffff8 77f80004 74380000 7b80008 10404000 a0000000
endmodule

module RWStage (
  input  [31:0] aluResult,
  input  [31:0] ldResult,
  input  isLd,
  input  [31:0] pc,
  input  isCall,
  input  [3:0] rd,
  output [31:0] Result,
  output [3:0] \reg 
);

  wire nor_1_out;
  wire [31:0] adder_1_out;

  nor nor_1 (nor_1_out, isLd, isCall);
  Multiplexer #(.width(4), .enable("false")) multiplexer_1 (.in0(rd), .in1(4'b1111), .out(\reg ), .sel(isCall));
  Adder #(.width(32)) adder_1 (.a(pc), .b(32'h4), .out(adder_1_out));  // open: cin, cout
  assign Result = nor_1_out ? aluResult : 32'bz;  // Controlled_Buffer controlled_buffer_1
  assign Result = isLd ? ldResult : 32'bz;  // Controlled_Buffer controlled_buffer_2
  assign Result = isCall ? adder_1_out : 32'bz;  // Controlled_Buffer controlled_buffer_3

  // Other names for the same wires on the sheet: a = isCall
endmodule

module MAStage (
  input  [31:0] MDR,
  input  isSt,
  input  [31:0] MAR,
  output [31:0] ldResult
);

  wire and_1_out, clock_1_out, not_1_out, not_2_out;
  wire [1:0] mod_3_counter_q;

  Clock clock_1 (.out(clock_1_out));
  Counter #(.width(2), .max('h2)) mod_3_counter (
    .Q(mod_3_counter_q), .clk(clock_1_out));  // open: load, D, count, carry, clr
  assign ldResult = isSt ? MDR : 32'bz;  // Controlled_Buffer controlled_buffer_1
  not not_1 (not_1_out, isSt);
  not not_2 (not_2_out, mod_3_counter_q[0]);
  and and_1 (and_1_out, not_2_out, mod_3_counter_q[1], isSt);
  RAM #(.addrWidth(24), .dataWidth(32)) ram_1 (
    .addr(MAR[23:0]), .data(ldResult), .clk(and_1_out), .ld(not_1_out));  // open: sel, clr

  // Other names for the same wires on the sheet: a = isSt
endmodule

module OFStage (
  input  [31:0] Result,
  input  [31:0] Instruction,
  input  isRet,
  input  isWb,
  input  isStore,
  input  [3:0] \reg ,
  output [3:0] rd,
  output [31:0] memoryload,
  output [31:0] op1,
  output [31:0] op2
);

  wire and_1_out, and_2_out, and_3_out, clock_1_out, not_1_out, not_2_out, not_3_out, not_4_out;
  wire [1:0] mod_3_counter_q;
  wire [3:0] multiplexer_1_out, multiplexer_2_out, multiplexer_3_out;
  wire [31:0] demultiplexer_1_out0, demultiplexer_1_out1;

  Clock clock_1 (.out(clock_1_out));
  Counter #(.width(2), .max('h2)) mod_3_counter (
    .Q(mod_3_counter_q), .clk(clock_1_out));  // open: load, D, count, carry, clr
  Multiplexer #(.width(4), .enable("false")) multiplexer_1 (
    .in0(Instruction[21:18]), .in1(4'b1111), .out(multiplexer_1_out), .sel(isRet));
  Multiplexer #(.width(4), .enable("false")) multiplexer_2 (
    .in0(Instruction[17:14]), .in1(Instruction[25:22]), .out(multiplexer_2_out), .sel(isStore));
  Multiplexer #(.select(2), .width(4), .enable("false")) multiplexer_3 (
    .in0(multiplexer_1_out), .in1(multiplexer_2_out), .in2(\reg ), .out(multiplexer_3_out),
    .sel(mod_3_counter_q));  // open: in3
  not not_1 (not_1_out, mod_3_counter_q[0]);
  assign memoryload = and_1_out ? Result : 32'bz;  // Controlled_Buffer controlled_buffer_1
  and and_1 (and_1_out, not_1_out, mod_3_counter_q[1], isWb);
  not not_2 (not_2_out, mod_3_counter_q[1]);
  and and_2 (and_2_out, not_1_out, not_2_out);
  and and_3 (and_3_out, not_2_out, mod_3_counter_q[0]);
  not not_3 (not_3_out, and_1_out);
  RAM #(.addrWidth(4), .dataWidth(32), .bus("asynch")) ram_1 (
    .addr(multiplexer_3_out), .data(memoryload), .ld(not_3_out));  // open: sel, clr
  not not_4 (not_4_out, clock_1_out);
  Demultiplexer #(.select(2), .width(32), .enable("false")) demultiplexer_1 (
    .out0(demultiplexer_1_out0), .out1(demultiplexer_1_out1), .in(memoryload), .sel(mod_3_counter_q));  // open: out2, out3
  Register #(.width(32)) u_op1 (.D(demultiplexer_1_out0), .en(and_2_out), .Q(op1), .clk(not_4_out));  // open: clr
  Register #(.width(32)) u_op2 (.D(demultiplexer_1_out1), .en(and_3_out), .Q(op2), .clk(not_4_out));  // open: clr

  assign rd = Instruction[25:22];
endmodule

module clean_circ (
);

  wire isbeq, isbgt, isBranch, isCall, isimm, isLd, isRet, isSt, isUbranch, isWb;
  wire [3:0] rd, \reg ;
  wire [12:0] ALU_Signals;
  wire [31:0] A, AluResult, B, BranchTarget, Imm_and_Branch_immx, Instruction, MAStage_ldresult, op2, pc,
       Result;

  Clock clock_1 ();  // open: out
  IFStage IFStage (.BranchTarget(BranchTarget), .isBranchTaken(isBranch), .instruction(Instruction), .pc(pc));
  immAndBranchUnit Imm_and_Branch (
    .instruction(Instruction), .pc(pc), .value_of_ra(A), .isRet(isRet), .immx(Imm_and_Branch_immx),
    .BranchTarget(BranchTarget));
  Control_Unit Control_Unit (
    .I_bit(Instruction[26]), .opcode(Instruction[31:27]), .isSt(isSt), .isLd(isLd), .isBeq(isbeq),
    .isBgt(isbgt), .isRet(isRet), .isImmediate(isimm), .isWb(isWb), .isUbranch(isUbranch), .isCall(isCall),
    .ALUsignals(ALU_Signals));
  Multiplexer #(.width(32), .enable("false")) multiplexer_1 (
    .in0(op2), .in1(Imm_and_Branch_immx), .out(B), .sel(isimm));
  OFStage OFStage (
    .Result(Result), .Instruction(Instruction), .isWb(isWb), .rd(rd), .isRet(isRet), .isStore(isSt),
    .\reg (\reg ), .op1(A), .op2(op2));  // open: memoryload
  MAStage MAStage (.MDR(op2), .isSt(isSt), .MAR(AluResult), .ldResult(MAStage_ldresult));
  ALU ALU (
    .AluReasult(AluResult), .isUbranch(isUbranch), .isbgt(isbgt), .isbeq(isbeq), .isBranchTaken(isBranch),
    .op1(A), .op2(B), .ALu_Signals(ALU_Signals));
  RWStage RWStage (
    .aluResult(AluResult), .ldResult(MAStage_ldresult), .isLd(isLd), .pc(pc), .isCall(isCall), .rd(rd),
    .Result(Result), .\reg (\reg ));
endmodule
