// Logisim project branchUnit.circ as structural Verilog: 1 circuit, main circuit main
module main (
);

  wire GT, undriven;

  // AND_Gate and_1 has open pins: in0=GT, in1=undriven, out=open
endmodule
