// Logisim project mem.circ as structural Verilog: 3 circuits, main circuit main
module main (
  input  [23:0] in_1
);

  wire [31:0] rom_1_data;

  Clock clock_1 ();  // open: out
  ROM #(.addrWidth(24), .dataWidth(32)) rom_1 (.addr(in_1), .data(rom_1_data));  // open: sel
endmodule

module control_unit (
  input  [4:0] opcode,
  input  I_bit,
  output out_3,
  output out_4,
  output out_5,
  output out_6,
  output out_7
);


  assign out_3 = opcode[0];
  assign out_4 = opcode[1];
  assign out_5 = opcode[2];
  assign out_6 = opcode[3];
  assign out_7 = opcode[4];
endmodule

module IF_stage (
  input  [31:0] in_1,
  input  in_2,
  input  in_3,
  output [9:0] out_4,
  output [31:0] out_5,
  output [31:0] out_6
);

  wire clock_1_out;
  wire [31:0] adder_1_out;

  Clock clock_1 (.out(clock_1_out));
  Register #(.width(32)) register_1 (
    .D(adder_1_out), .Q({out_6[31:10], out_4}), .clk(clock_1_out), .clr(in_3));  // open: en
  main main_1 ();  // open: in_1
  Adder #(.width(32)) adder_1 (.a(in_1), .b({out_6[31:10], out_4}), .out(adder_1_out));  // open: cin, cout
  ROM #(.addrWidth(10), .dataWidth(32)) rom_1 (.addr(out_4), .data(out_5), .sel(in_2));

  assign out_6[9:0] = out_4;

  // Notes on the sheet:
  //   contents of rom_1 (hex, n*v repeats v):
  //   ffffffff f 1 11
endmodule
