// Logisim project mywork.circ as structural Verilog
module IF_stage (
  input  [31:0] BranchValue,
  input  isBranchTaken,
  input  reset,
  output [31:0] instruction,
  output [31:0] pc
);

  wire and_1_out, clock_out;
  wire [1:0] mod_3_counter_q;
  wire [31:0] adder_1_out, multiplexer_1_out;

  Clock clock (.out(clock_out));
  Counter #(.width(2), .max('h2)) mod_3_counter (
    .Q(mod_3_counter_q), .clk(clock_out));  // open: load, D, count, carry, clr
  and and_1 (and_1_out, mod_3_counter_q[0], mod_3_counter_q[1]);
  Register #(.width(32)) register_1 (.D(multiplexer_1_out), .Q(pc), .clk(and_1_out), .clr(reset));  // open: en
  Multiplexer #(.width(32)) multiplexer_1 (
    .in0(adder_1_out), .in1(BranchValue), .out(multiplexer_1_out), .sel(isBranchTaken));  // open: en
  Adder #(.width(32)) adder_1 (.a(32'h4), .b(pc), .out(adder_1_out));  // open: cin, cout
  ROM #(.addrWidth(10), .dataWidth(32)) rom_1 (.addr(pc[11:2]), .data(instruction));  // open: sel

  // Notes on the sheet:
  //   contents of rom_1 (hex, n*v repeats v):
  //   fffffff0 f 1 11
endmodule

module RW_stage (
  input  [31:0] aluResult,
  input  [31:0] ldResult,
  input  isLd,
  input  [31:0] pc,
  input  isCall,
  input  [3:0] rd,
  output [31:0] Result,
  output [3:0] \reg 
);

  wire nor_1_out;
  wire [31:0] adder_1_out;

  nor nor_1 (nor_1_out, isLd, isCall);
  Multiplexer #(.width(4), .enable("false")) multiplexer_1 (.in0(rd), .in1(4'b1111), .out(\reg ), .sel(isCall));
  Adder #(.width(32)) adder_1 (.a(pc), .b(32'h4), .out(adder_1_out));  // open: cin, cout
  assign Result = nor_1_out ? aluResult : 32'bz;  // Controlled_Buffer controlled_buffer_1
  assign Result = isLd ? ldResult : 32'bz;  // Controlled_Buffer controlled_buffer_2
  assign Result = isCall ? adder_1_out : 32'bz;  // Controlled_Buffer controlled_buffer_3

  // Other names for the same wires on the sheet: a = isCall
endmodule

module MA_stage (
  input  [31:0] MDR,
  input  isSt,
  input  [31:0] MAR,
  output [31:0] ldResult
);

  wire and_1_out, clock_out, not_1_out, not_2_out;
  wire [1:0] mod_3_counter_q;

  Clock clock (.out(clock_out));
  assign ldResult = isSt ? MDR : 32'bz;  // Controlled_Buffer controlled_buffer_1
  Counter #(.width(2), .max('h2)) mod_3_counter (
    .Q(mod_3_counter_q), .clk(clock_out));  // open: load, D, count, carry, clr
  not not_1 (not_1_out, isSt);
  not not_2 (not_2_out, mod_3_counter_q[0]);
  and and_1 (and_1_out, not_2_out, mod_3_counter_q[1], isSt);
  RAM #(.addrWidth(24), .dataWidth(32)) ram_1 (
    .addr(MAR[23:0]), .data(ldResult), .clk(and_1_out), .ld(not_1_out));  // open: sel, clr

  // Other names for the same wires on the sheet: a = isSt
endmodule

module imm_and_branch_unit (
  input  [31:0] instruction,
  input  [31:0] pc,
  input  [31:0] value_of_ra,
  input  isRet,
  output [31:0] immx,
  output [31:0] BranchTarget
);

  wire [31:0] adder_1_out, bit_extender_2_out;

  assign immx = {{14{instruction[17]}}, instruction[17:0]};  // Bit_Extender bit_extender_1
  assign bit_extender_2_out = {{3{instruction[26]}}, {instruction[26:0], 2'b00}};  // Bit_Extender bit_extender_2
  Adder #(.width(32)) adder_1 (.a(bit_extender_2_out), .b(pc), .out(adder_1_out));  // open: cin, cout
  Multiplexer #(.width(32)) multiplexer_1 (
    .in0(adder_1_out), .in1(value_of_ra), .out(BranchTarget), .sel(isRet));  // open: en
endmodule

module OF_stage (
  input  [31:0] Result,
  input  [31:0] Instruction,
  input  isRet,
  input  isWb,
  input  isStore,
  input  [3:0] \reg ,
  input  in_7,
  output [3:0] rd,
  output [31:0] memoryload,
  output [1:0] out_10,
  output [31:0] op1,
  output [31:0] op2
);

  wire and_1_out, and_2_out, and_3_out, clock_out, not_1_out, not_2_out, not_3_out;
  wire [3:0] multiplexer_1_out, multiplexer_2_out, multiplexer_3_out;
  wire [31:0] demultiplexer_1_out0, demultiplexer_1_out1;

  Clock clock (.out(clock_out));
  Counter #(.width(2), .max('h2)) mod_3_counter (
    .Q(out_10), .clk(clock_out), .clr(in_7));  // open: load, D, count, carry
  Multiplexer #(.width(4), .enable("false")) multiplexer_1 (
    .in0(Instruction[21:18]), .in1(4'b1111), .out(multiplexer_1_out), .sel(isRet));
  Multiplexer #(.width(4), .enable("false")) multiplexer_2 (
    .in0(Instruction[17:14]), .in1(Instruction[25:22]), .out(multiplexer_2_out), .sel(isStore));
  Multiplexer #(.select(2), .width(4), .enable("false")) multiplexer_3 (
    .in0(multiplexer_1_out), .in1(multiplexer_2_out), .in2(\reg ), .out(multiplexer_3_out), .sel(out_10));  // open: in3
  not not_1 (not_1_out, out_10[0]);
  and and_1 (and_1_out, not_1_out, out_10[1], isWb);
  not not_2 (not_2_out, out_10[1]);
  assign memoryload = and_1_out ? Result : 32'bz;  // Controlled_Buffer controlled_buffer_1
  and and_2 (and_2_out, not_1_out, not_2_out);
  and and_3 (and_3_out, not_2_out, out_10[0]);
  not not_3 (not_3_out, and_1_out);
  RAM #(.addrWidth(4), .dataWidth(32)) ram_1 (
    .addr(multiplexer_3_out), .data(memoryload), .clk(clock_out), .ld(not_3_out));  // open: sel, clr
  Demultiplexer #(.select(2), .width(32), .enable("false")) demultiplexer_1 (
    .out0(demultiplexer_1_out0), .out1(demultiplexer_1_out1), .in(memoryload), .sel(out_10));  // open: out2, out3
  Register #(.width(32)) u_op1 (.D(demultiplexer_1_out0), .en(and_2_out), .Q(op1), .clk(clock_out));  // open: clr
  Register #(.width(32)) u_op2 (.D(demultiplexer_1_out1), .en(and_3_out), .Q(op2), .clk(clock_out));  // open: clr

  assign rd = Instruction[25:22];
endmodule

module Control_Unit (
  input  I_bit,
  input  [4:0] opcode,
  output isSt,
  output isLd,
  output isBeq,
  output isBgt,
  output isRet,
  output isImmediate,
  output isWb,
  output isUbranch,
  output isCall,
  output [12:0] ALUsignals
);

  wire and_6_out, and_7_out, and_8_out, and_9_out, and_10_out, and_12_out, and_13_out, nand_1_out;

  nand nand_1 (nand_1_out, opcode[0], opcode[1]);
  and and_1 (isSt, opcode[0], opcode[1], opcode[2], opcode[3], ~opcode[4]);  // AND_Gate
  and and_2 (isLd, ~opcode[0], opcode[1], opcode[2], opcode[3], ~opcode[4]);  // AND_Gate
  and and_3 (isBeq, ~opcode[0], ~opcode[1], ~opcode[2], ~opcode[3], opcode[4]);  // AND_Gate
  and and_4 (isBgt, opcode[0], ~opcode[1], ~opcode[2], ~opcode[3], opcode[4]);  // AND_Gate
  and and_5 (isRet, ~opcode[0], ~opcode[1], opcode[2], ~opcode[3], opcode[4]);  // AND_Gate
  and and_6 (and_6_out, opcode[0], ~opcode[1], opcode[2], ~opcode[4]);  // AND_Gate
  and and_7 (and_7_out, opcode[0], opcode[2], opcode[3], ~opcode[4]);  // AND_Gate
  and and_8 (and_8_out, opcode[4], nand_1_out);
  and and_9 (and_9_out, opcode[1], ~opcode[2], ~opcode[3], opcode[4]);  // AND_Gate
  and and_10 (and_10_out, ~opcode[0], ~opcode[1], opcode[2], ~opcode[3], opcode[4]);  // AND_Gate
  and and_11 (isCall, opcode[0], opcode[1], ~opcode[2], ~opcode[3], opcode[4]);  // AND_Gate
  and and_12 (and_12_out, ~opcode[0], ~opcode[1], ~opcode[2], ~opcode[3], ~opcode[4]);  // AND_Gate
  and and_13 (and_13_out, opcode[1], opcode[2], opcode[3], ~opcode[4]);  // AND_Gate
  and isSub (ALUsignals[2], opcode[0], ~opcode[1], ~opcode[2], ~opcode[3], ~opcode[4]);  // AND_Gate
  and isCmp (ALUsignals[0], opcode[0], ~opcode[1], opcode[2], ~opcode[3], ~opcode[4]);  // AND_Gate
  and isMul (ALUsignals[3], ~opcode[0], opcode[1], ~opcode[2], ~opcode[3], ~opcode[4]);  // AND_Gate
  and isDiv (ALUsignals[4], opcode[0], opcode[1], ~opcode[2], ~opcode[3], ~opcode[4]);  // AND_Gate
  and isMod (ALUsignals[5], ~opcode[0], ~opcode[1], opcode[2], ~opcode[3], ~opcode[4]);  // AND_Gate
  and isLsl (ALUsignals[7], ~opcode[0], opcode[1], ~opcode[2], opcode[3], ~opcode[4]);  // AND_Gate
  and isLsr (ALUsignals[8], opcode[0], opcode[1], ~opcode[2], opcode[3], ~opcode[4]);  // AND_Gate
  and isAsr (ALUsignals[9], ~opcode[0], ~opcode[1], opcode[2], opcode[3], ~opcode[4]);  // AND_Gate
  and isOr (ALUsignals[12], opcode[0], opcode[1], opcode[2], ~opcode[3], ~opcode[4]);  // AND_Gate
  and isAnd (ALUsignals[11], ~opcode[0], opcode[1], opcode[2], ~opcode[3], ~opcode[4]);  // AND_Gate
  and isNot (ALUsignals[10], ~opcode[0], ~opcode[1], ~opcode[2], opcode[3], ~opcode[4]);  // AND_Gate
  and isMov (ALUsignals[6], opcode[0], ~opcode[1], ~opcode[2], opcode[3], ~opcode[4]);  // AND_Gate
  nor nor_1 (isWb, and_6_out, and_7_out, and_8_out);
  or or_1 (isUbranch, and_9_out, and_10_out);
  or isAdd (ALUsignals[1], and_12_out, and_13_out);

  assign isImmediate = I_bit;

  // Notes on the sheet:
  //   op1
  //   op2
  //   op3
  //   op4
  //   op5
endmodule
